# Fritzing sketch leituraDigital (saved by Fritzing 0.9.3b)
breadboards: 1

parts:
  S1 = Pushbutton [package="[THT]"]
  Componente1 = Arduino Uno (Rev3)
  S2 = Pushbutton [package="[THT]"]
  LED1 = LED - 5mm [color="Red (633nm)" package="5 mm [THT]"]
  R1 = Resistor [tolerance=±5% resistance=220 package=THT]
  R2 = Resistor [tolerance=±5% resistance=10k package=THT]
  R3 = Resistor [tolerance=±5% resistance=10k package=THT]

nets:
  N1: S1.Pin_1, S1.Pin_2, Componente1.D4, R3.Pin_1
  N2: S1.Pin_3, S1.Pin_4, Componente1.5V, S2.Pin_3, S2.Pin_4
  N3: Componente1.D13/SCK, LED1.anode
  N4: Componente1.GND, R1.Pin_1, R2.Pin_0, R3.Pin_0
  N5: Componente1.D2, S2.Pin_1, S2.Pin_2, R2.Pin_1
  N6: LED1.cathode, R1.Pin_0
