# Fritzing sketch atividade1 (saved by Fritzing 0.9.3b)
breadboards: 1

parts:
  Componente1 = Arduino Uno (Rev3)
  hc-sr1 = hc-sr04
  R1 = Resistor [tolerance=±5% resistance=220 package=THT]
  LED1 = LED - 5mm [color="Red (633nm)" package="5 mm [THT]"]

nets:
  N1: Componente1.D8, LED1.anode
  5V: Componente1.5V, hc-sr1.VCC
  GND: Componente1.GND, hc-sr1.GND, R1.Pin_0
  N2: R1.Pin_1, LED1.cathode
