# Fritzing sketch motor (saved by Fritzing 0.9.3b)
breadboards: 2

parts:
  S1 = Toggle Switch [package=THT]
  M1 = DC Motor
  M2 = DC Motor
  VCC1 = Battery block 9V

nets:
  N1: S1.L1, M1.pin_1, M2.pin_1
  N2: S1.COM, VCC1.+
  N3: M1.pin_2, M2.pin_2, VCC1.-
