# Fritzing sketch robo (saved by Fritzing 0.9.3b)
breadboards: 2

parts:
  S1 = Toggle Switch [package=THT]
  M1 = DC Motor
  M2 = DC Motor
  VCC1 = Battery block 9V
  IC1 = L293D [package=THT]
  Componente1 = Arduino Uno (Rev3)
  hc-sr1 = hc-sr04

nets:
  N1: S1.L1, IC1.+Vmotor, Componente1.VIN
  N2: S1.COM, VCC1.+
  N3: M1.pin_1, IC1.Out_4_(_Controlled_by_Enable_2_)
  N4: M1.pin_2, IC1.Out_3_(_Controlled_by_Enable_2_)
  N5: M2.pin_1, IC1.Out_2_(_Controlled_by_Enable_1_)
  N6: M2.pin_2, IC1.Out_1_(_Controlled_by_Enable_1_)
  GND: VCC1.-, IC1.0V, Componente1.GND, hc-sr1.GND
  5V: IC1.Enable_1, IC1.Enable_2, IC1.+V, Componente1.5V, hc-sr1.VCC
  N7: IC1.In_1, Componente1.D9_PWM
  N8: IC1.In_2, Componente1.D10_PWM/SS
  N9: IC1.In_3, Componente1.D5_PWM
  N10: IC1.In_4, Componente1.D6_PWM
  N11: Componente1.D12/MISO, hc-sr1.Trig
  N12: Componente1.D13/SCK, hc-sr1.Echo
